// Logisim project Exercice_3_1_additionneur.circ as structural Verilog: 7 circuits, main circuit main
module main (
  input  A,
  input  B,
  input  Cin,
  output O,
  output Cout
);

  wire and_1_out, and_2_out, and_3_out, and_4_out, and_5_out, and_6_out, and_7_out, and_8_out, not_1_out,
       not_2_out, not_3_out;

  not not_1 (not_1_out, A);
  not not_2 (not_2_out, B);
  not not_3 (not_3_out, Cin);
  and and_1 (and_1_out, not_1_out, not_2_out, Cin);
  and and_2 (and_2_out, not_1_out, B, not_3_out);
  and and_3 (and_3_out, A, not_2_out, not_3_out);
  and and_4 (and_4_out, A, B, Cin);
  and and_5 (and_5_out, not_1_out, B, Cin);
  and and_6 (and_6_out, A, not_2_out, Cin);
  and and_7 (and_7_out, A, B, not_3_out);
  and and_8 (and_8_out, A, B, Cin);
  or or_1 (O, and_1_out, and_2_out, and_3_out, and_4_out);
  or or_2 (Cout, and_5_out, and_6_out, and_7_out, and_8_out);
endmodule

module adder_1bit (
  input  in_1,
  input  in_2,
  input  in_3,
  output out_4,
  output out_5
);

  main main_1 (.A(in_1), .B(in_2), .Cin(in_3), .O(out_4), .Cout(out_5));
endmodule

module adder_2bits (
  input  A0,
  input  B0,
  input  Cin,
  input  A1,
  input  B1,
  output O0,
  output O1,
  output Cout
);

  wire adder_1bit_1_out_5;

  adder_1bit adder_1bit_1 (.in_1(A0), .in_2(B0), .in_3(Cin), .out_4(O0), .out_5(adder_1bit_1_out_5));
  adder_1bit adder_1bit_2 (.in_1(A1), .in_2(B1), .in_3(adder_1bit_1_out_5), .out_4(O1), .out_5(Cout));
endmodule

module adder_4bits (
  input  A0,
  input  B0,
  input  Cin,
  input  A1,
  input  B1,
  input  A2,
  input  B2,
  input  A3,
  input  B3,
  output O0,
  output O1,
  output O2,
  output O3,
  output Cout
);

  wire adder_2bits_1_cout;

  adder_2bits adder_2bits_1 (
    .A0(A0), .B0(B0), .Cin(Cin), .A1(A1), .B1(B1), .O0(O0), .O1(O1), .Cout(adder_2bits_1_cout));
  adder_2bits adder_2bits_2 (
    .A0(A2), .B0(B2), .Cin(adder_2bits_1_cout), .A1(A3), .B1(B3), .O0(O2), .O1(O3), .Cout(Cout));
endmodule

module adder_8bits (
  input  A0,
  input  B0,
  input  A1,
  input  B1,
  input  A2,
  input  B2,
  input  A3,
  input  B3,
  input  A4,
  input  B4,
  input  A5,
  input  B5,
  input  A6,
  input  B6,
  input  A7,
  input  B7,
  input  Cin,
  output O0,
  output O1,
  output O2,
  output O3,
  output O4,
  output O5,
  output O6,
  output O7,
  output Cout
);

  wire adder_4bits_1_cout;

  adder_4bits adder_4bits_1 (
    .A0(A0), .B0(B0), .Cin(Cin), .A1(A1), .B1(B1), .A2(A2), .B2(B2), .A3(A3), .B3(B3), .O0(O0), .O1(O1),
    .O2(O2), .O3(O3), .Cout(adder_4bits_1_cout));
  adder_4bits adder_4bits_2 (
    .A0(A4), .B0(B4), .Cin(adder_4bits_1_cout), .A1(A5), .B1(B5), .A2(A6), .B2(B6), .A3(A7), .B3(B7),
    .O0(O4), .O1(O5), .O2(O6), .O3(O7), .Cout(Cout));
endmodule

module adder_16bits (
  input  A0,
  input  B0,
  input  A1,
  input  B1,
  input  A2,
  input  B2,
  input  A3,
  input  B3,
  input  A4,
  input  B4,
  input  A5,
  input  B5,
  input  A6,
  input  B6,
  input  A7,
  input  B7,
  input  A8,
  input  B8,
  input  A9,
  input  B9,
  input  A10,
  input  B10,
  input  A11,
  input  B11,
  input  A12,
  input  B12,
  input  A13,
  input  B13,
  input  A14,
  input  B14,
  input  A15,
  input  B15,
  input  Cin,
  output O0,
  output O1,
  output O2,
  output O3,
  output O4,
  output O5,
  output O6,
  output O7,
  output O8,
  output O9,
  output O10,
  output O11,
  output O12,
  output O13,
  output O14,
  output O15,
  output Cout
);

  wire adder_8bits_1_cout;

  adder_8bits adder_8bits_1 (
    .A0(A0), .B0(B0), .A1(A1), .B1(B1), .A2(A2), .B2(B2), .A3(A3), .B3(B3), .A4(A4), .B4(B4), .A5(A5),
    .B5(B5), .A6(A6), .B6(B6), .A7(A7), .B7(B7), .Cin(Cin), .O0(O0), .O1(O1), .O2(O2), .O3(O3), .O4(O4),
    .O5(O5), .O6(O6), .O7(O7), .Cout(adder_8bits_1_cout));
  adder_8bits adder_8bits_2 (
    .A0(A8), .B0(B8), .A1(A9), .B1(B9), .A2(A10), .B2(B10), .A3(A11), .B3(B11), .A4(A12), .B4(B12), .A5(A13),
    .B5(B13), .A6(A14), .B6(B14), .A7(A15), .B7(B15), .Cin(adder_8bits_1_cout), .O0(O8), .O1(O9), .O2(O10),
    .O3(O11), .O4(O12), .O5(O13), .O6(O14), .O7(O15), .Cout(Cout));
endmodule

module adder_32bits (
  input  A0,
  input  B0,
  input  A1,
  input  B1,
  input  A2,
  input  B2,
  input  A3,
  input  B3,
  input  A4,
  input  B4,
  input  A5,
  input  B5,
  input  A6,
  input  B6,
  input  A7,
  input  B7,
  input  A8,
  input  B8,
  input  A9,
  input  B9,
  input  A10,
  input  B10,
  input  A11,
  input  B11,
  input  A12,
  input  B12,
  input  A13,
  input  B13,
  input  A14,
  input  B14,
  input  A15,
  input  B15,
  input  A16,
  input  B16,
  input  A17,
  input  B17,
  input  A18,
  input  B18,
  input  A19,
  input  B19,
  input  A20,
  input  B20,
  input  A21,
  input  B21,
  input  A22,
  input  B22,
  input  A23,
  input  B23,
  input  A24,
  input  B24,
  input  A25,
  input  B25,
  input  A26,
  input  B26,
  input  A27,
  input  B27,
  input  A28,
  input  B28,
  input  A29,
  input  B29,
  input  A30,
  input  B30,
  input  A31,
  input  B31,
  input  Cin,
  output O0,
  output O1,
  output O2,
  output O3,
  output O4,
  output O5,
  output O6,
  output O7,
  output O8,
  output O9,
  output O10,
  output O11,
  output O12,
  output O13,
  output O14,
  output O15,
  output O16,
  output O17,
  output O18,
  output O19,
  output O20,
  output O21,
  output O22,
  output O23,
  output O24,
  output O25,
  output O26,
  output O27,
  output O28,
  output O29,
  output O30,
  output O31,
  output Cout
);

  wire adder_16bits_1_cout;

  adder_16bits adder_16bits_1 (
    .A0(A0), .B0(B0), .A1(A1), .B1(B1), .A2(A2), .B2(B2), .A3(A3), .B3(B3), .A4(A4), .B4(B4), .A5(A5),
    .B5(B5), .A6(A6), .B6(B6), .A7(A7), .B7(B7), .A8(A8), .B8(B8), .A9(A9), .B9(B9), .A10(A10), .B10(B10),
    .A11(A11), .B11(B11), .A12(A12), .B12(B12), .A13(A13), .B13(B13), .A14(A14), .B14(B14), .A15(A15),
    .B15(B15), .Cin(Cin), .O0(O0), .O1(O1), .O2(O2), .O3(O3), .O4(O4), .O5(O5), .O6(O6), .O7(O7), .O8(O8),
    .O9(O9), .O10(O10), .O11(O11), .O12(O12), .O13(O13), .O14(O14), .O15(O15), .Cout(adder_16bits_1_cout));
  adder_16bits adder_16bits_2 (
    .A0(A16), .B0(B16), .A1(A17), .B1(B17), .A2(A18), .B2(B18), .A3(A19), .B3(B19), .A4(A20), .B4(B20),
    .A5(A21), .B5(B21), .A6(A22), .B6(B22), .A7(A23), .B7(B23), .A8(A24), .B8(B24), .A9(A25), .B9(B25),
    .A10(A26), .B10(B26), .A11(A27), .B11(B27), .A12(A28), .B12(B28), .A13(A29), .B13(B29), .A14(A30),
    .B14(B30), .A15(A31), .B15(B31), .Cin(adder_16bits_1_cout), .O0(O16), .O1(O17), .O2(O18), .O3(O19),
    .O4(O20), .O5(O21), .O6(O22), .O7(O23), .O8(O24), .O9(O25), .O10(O26), .O11(O27), .O12(O28), .O13(O29),
    .O14(O30), .O15(O31), .Cout(Cout));
endmodule
