// Logisim project Exercice_3_1_soustracteur.circ as structural Verilog: 8 circuits, main circuit main
module main (
  input  A,
  input  B,
  input  Cin,
  output O,
  output Cout
);

  wire and_1_out, and_2_out, and_3_out, and_4_out, and_5_out, and_6_out, and_7_out, and_8_out, not_1_out,
       not_2_out, not_3_out;

  not not_1 (not_1_out, A);
  not not_2 (not_2_out, B);
  not not_3 (not_3_out, Cin);
  and and_1 (and_1_out, not_1_out, not_2_out, Cin);
  and and_2 (and_2_out, not_1_out, B, not_3_out);
  and and_3 (and_3_out, A, not_2_out, not_3_out);
  and and_4 (and_4_out, A, B, Cin);
  and and_5 (and_5_out, not_1_out, B, Cin);
  and and_6 (and_6_out, A, not_2_out, Cin);
  and and_7 (and_7_out, A, B, not_3_out);
  and and_8 (and_8_out, A, B, Cin);
  or or_1 (O, and_1_out, and_2_out, and_3_out, and_4_out);
  or or_2 (Cout, and_5_out, and_6_out, and_7_out, and_8_out);

  // Notes on the sheet:
  //   CIRCUIT DE O[0]
endmodule

module adder_1bit (
  input  in_1,
  input  in_2,
  input  in_3,
  output out_4,
  output out_5
);

  main main_1 (.A(in_1), .B(in_2), .Cin(in_3), .O(out_4), .Cout(out_5));
endmodule

module adder_2bits (
  input  A0,
  input  B0,
  input  Cin,
  input  A1,
  input  B1,
  output O0,
  output O1,
  output Cout
);

  wire adder_1bit_1_out_5;

  adder_1bit adder_1bit_1 (.in_1(A0), .in_2(B0), .in_3(Cin), .out_4(O0), .out_5(adder_1bit_1_out_5));
  adder_1bit adder_1bit_2 (.in_1(A1), .in_2(B1), .in_3(adder_1bit_1_out_5), .out_4(O1), .out_5(Cout));
endmodule

module adder_4bits (
  input  A0,
  input  B0,
  input  Cin,
  input  A1,
  input  B1,
  input  A2,
  input  B2,
  input  A3,
  input  B3,
  output O0,
  output O1,
  output O2,
  output O3,
  output Cout
);

  wire adder_2bits_1_cout;

  adder_2bits adder_2bits_1 (
    .A0(A0), .B0(B0), .Cin(Cin), .A1(A1), .B1(B1), .O0(O0), .O1(O1), .Cout(adder_2bits_1_cout));
  adder_2bits adder_2bits_2 (
    .A0(A2), .B0(B2), .Cin(adder_2bits_1_cout), .A1(A3), .B1(B3), .O0(O2), .O1(O3), .Cout(Cout));
endmodule

module adder_8bits (
  input  A0,
  input  B0,
  input  A1,
  input  B1,
  input  A2,
  input  B2,
  input  A3,
  input  B3,
  input  A4,
  input  B4,
  input  A5,
  input  B5,
  input  A6,
  input  B6,
  input  A7,
  input  B7,
  input  Cin,
  output O0,
  output O1,
  output O2,
  output O3,
  output O4,
  output O5,
  output O6,
  output O7,
  output Cout
);

  wire adder_4bits_1_cout;

  adder_4bits adder_4bits_1 (
    .A0(A0), .B0(B0), .Cin(Cin), .A1(A1), .B1(B1), .A2(A2), .B2(B2), .A3(A3), .B3(B3), .O0(O0), .O1(O1),
    .O2(O2), .O3(O3), .Cout(adder_4bits_1_cout));
  adder_4bits adder_4bits_2 (
    .A0(A4), .B0(B4), .Cin(adder_4bits_1_cout), .A1(A5), .B1(B5), .A2(A6), .B2(B6), .A3(A7), .B3(B7),
    .O0(O4), .O1(O5), .O2(O6), .O3(O7), .Cout(Cout));
endmodule

module adder_16bits (
  input  A0,
  input  B0,
  input  A1,
  input  B1,
  input  A2,
  input  B2,
  input  A3,
  input  B3,
  input  A4,
  input  B4,
  input  A5,
  input  B5,
  input  A6,
  input  B6,
  input  A7,
  input  B7,
  input  A8,
  input  B8,
  input  A9,
  input  B9,
  input  A10,
  input  B10,
  input  A11,
  input  B11,
  input  A12,
  input  B12,
  input  A13,
  input  B13,
  input  A14,
  input  B14,
  input  A15,
  input  B15,
  input  Cin,
  output O0,
  output O1,
  output O2,
  output O3,
  output O4,
  output O5,
  output O6,
  output O7,
  output O8,
  output O9,
  output O10,
  output O11,
  output O12,
  output O13,
  output O14,
  output O15,
  output Cout
);

  wire adder_8bits_1_cout;

  adder_8bits adder_8bits_1 (
    .A0(A0), .B0(B0), .A1(A1), .B1(B1), .A2(A2), .B2(B2), .A3(A3), .B3(B3), .A4(A4), .B4(B4), .A5(A5),
    .B5(B5), .A6(A6), .B6(B6), .A7(A7), .B7(B7), .Cin(Cin), .O0(O0), .O1(O1), .O2(O2), .O3(O3), .O4(O4),
    .O5(O5), .O6(O6), .O7(O7), .Cout(adder_8bits_1_cout));
  adder_8bits adder_8bits_2 (
    .A0(A8), .B0(B8), .A1(A9), .B1(B9), .A2(A10), .B2(B10), .A3(A11), .B3(B11), .A4(A12), .B4(B12), .A5(A13),
    .B5(B13), .A6(A14), .B6(B14), .A7(A15), .B7(B15), .Cin(adder_8bits_1_cout), .O0(O8), .O1(O9), .O2(O10),
    .O3(O11), .O4(O12), .O5(O13), .O6(O14), .O7(O15), .Cout(Cout));
endmodule

module adder_32bits (
  input  A0,
  input  B0,
  input  A1,
  input  B1,
  input  A2,
  input  B2,
  input  A3,
  input  B3,
  input  A4,
  input  B4,
  input  A5,
  input  B5,
  input  A6,
  input  B6,
  input  A7,
  input  B7,
  input  A8,
  input  B8,
  input  A9,
  input  B9,
  input  A10,
  input  B10,
  input  A11,
  input  B11,
  input  A12,
  input  B12,
  input  A13,
  input  B13,
  input  A14,
  input  B14,
  input  A15,
  input  B15,
  input  A16,
  input  B16,
  input  A17,
  input  B17,
  input  A18,
  input  B18,
  input  A19,
  input  B19,
  input  A20,
  input  B20,
  input  A21,
  input  B21,
  input  A22,
  input  B22,
  input  A23,
  input  B23,
  input  A24,
  input  B24,
  input  A25,
  input  B25,
  input  A26,
  input  B26,
  input  A27,
  input  B27,
  input  A28,
  input  B28,
  input  A29,
  input  B29,
  input  A30,
  input  B30,
  input  A31,
  input  B31,
  input  Cin,
  output O0,
  output O1,
  output O2,
  output O3,
  output O4,
  output O5,
  output O6,
  output O7,
  output O8,
  output O9,
  output O10,
  output O11,
  output O12,
  output O13,
  output O14,
  output O15,
  output O16,
  output O17,
  output O18,
  output O19,
  output O20,
  output O21,
  output O22,
  output O23,
  output O24,
  output O25,
  output O26,
  output O27,
  output O28,
  output O29,
  output O30,
  output O31,
  output Cout
);

  wire adder_16bits_1_cout;

  adder_16bits adder_16bits_1 (
    .A0(A0), .B0(B0), .A1(A1), .B1(B1), .A2(A2), .B2(B2), .A3(A3), .B3(B3), .A4(A4), .B4(B4), .A5(A5),
    .B5(B5), .A6(A6), .B6(B6), .A7(A7), .B7(B7), .A8(A8), .B8(B8), .A9(A9), .B9(B9), .A10(A10), .B10(B10),
    .A11(A11), .B11(B11), .A12(A12), .B12(B12), .A13(A13), .B13(B13), .A14(A14), .B14(B14), .A15(A15),
    .B15(B15), .Cin(Cin), .O0(O0), .O1(O1), .O2(O2), .O3(O3), .O4(O4), .O5(O5), .O6(O6), .O7(O7), .O8(O8),
    .O9(O9), .O10(O10), .O11(O11), .O12(O12), .O13(O13), .O14(O14), .O15(O15), .Cout(adder_16bits_1_cout));
  adder_16bits adder_16bits_2 (
    .A0(A16), .B0(B16), .A1(A17), .B1(B17), .A2(A18), .B2(B18), .A3(A19), .B3(B19), .A4(A20), .B4(B20),
    .A5(A21), .B5(B21), .A6(A22), .B6(B22), .A7(A23), .B7(B23), .A8(A24), .B8(B24), .A9(A25), .B9(B25),
    .A10(A26), .B10(B26), .A11(A27), .B11(B27), .A12(A28), .B12(B28), .A13(A29), .B13(B29), .A14(A30),
    .B14(B30), .A15(A31), .B15(B31), .Cin(adder_16bits_1_cout), .O0(O16), .O1(O17), .O2(O18), .O3(O19),
    .O4(O20), .O5(O21), .O6(O22), .O7(O23), .O8(O24), .O9(O25), .O10(O26), .O11(O27), .O12(O28), .O13(O29),
    .O14(O30), .O15(O31), .Cout(Cout));
endmodule

module soustracteur_32bits (
  input  A0,
  input  B0,
  input  A1,
  input  B1,
  input  A2,
  input  B2,
  input  A3,
  input  B3,
  input  A4,
  input  B4,
  input  A5,
  input  B5,
  input  A6,
  input  B6,
  input  A7,
  input  B7,
  input  A8,
  input  B8,
  input  A9,
  input  B9,
  input  A10,
  input  B10,
  input  A11,
  input  B11,
  input  A12,
  input  B12,
  input  A13,
  input  B13,
  input  A14,
  input  B14,
  input  A15,
  input  B15,
  input  A16,
  input  B16,
  input  A17,
  input  B17,
  input  A18,
  input  B18,
  input  A19,
  input  B19,
  input  A20,
  input  B20,
  input  A21,
  input  B21,
  input  A22,
  input  B22,
  input  A23,
  input  B23,
  input  A24,
  input  B24,
  input  A25,
  input  B25,
  input  A26,
  input  B26,
  input  A27,
  input  B27,
  input  A28,
  input  B28,
  input  A29,
  input  B29,
  input  A30,
  input  B30,
  input  A31,
  input  B31,
  input  Cin,
  output O0,
  output O1,
  output O2,
  output O3,
  output O4,
  output O5,
  output O6,
  output O7,
  output O8,
  output O9,
  output O10,
  output O11,
  output O12,
  output O13,
  output O14,
  output O15,
  output O16,
  output O17,
  output O18,
  output O19,
  output O20,
  output O21,
  output O22,
  output O23,
  output O24,
  output O25,
  output O26,
  output O27,
  output O28,
  output O29,
  output O30,
  output O31,
  output Cout
);

  wire xor_1_out, xor_2_out, xor_3_out, xor_4_out, xor_5_out, xor_6_out, xor_7_out, xor_8_out, xor_9_out,
       xor_10_out, xor_11_out, xor_12_out, xor_13_out, xor_14_out, xor_15_out, xor_16_out, xor_17_out,
       xor_18_out, xor_19_out, xor_20_out, xor_21_out, xor_22_out, xor_23_out, xor_24_out, xor_25_out,
       xor_26_out, xor_27_out, xor_28_out, xor_29_out, xor_30_out, xor_31_out, xor_32_out;

  xor xor_1 (xor_1_out, B0, Cin);
  xor xor_2 (xor_2_out, B1, Cin);
  xor xor_3 (xor_3_out, B2, Cin);
  xor xor_4 (xor_4_out, B3, Cin);
  xor xor_5 (xor_5_out, B4, Cin);
  xor xor_6 (xor_6_out, B5, Cin);
  xor xor_7 (xor_7_out, B6, Cin);
  xor xor_8 (xor_8_out, B7, Cin);
  xor xor_9 (xor_9_out, B8, Cin);
  xor xor_10 (xor_10_out, B9, Cin);
  xor xor_11 (xor_11_out, B10, Cin);
  xor xor_12 (xor_12_out, B11, Cin);
  xor xor_13 (xor_13_out, B12, Cin);
  xor xor_14 (xor_14_out, B13, Cin);
  xor xor_15 (xor_15_out, B14, Cin);
  xor xor_16 (xor_16_out, B15, Cin);
  xor xor_17 (xor_17_out, B16, Cin);
  xor xor_18 (xor_18_out, B17, Cin);
  xor xor_19 (xor_19_out, B18, Cin);
  xor xor_20 (xor_20_out, B19, Cin);
  xor xor_21 (xor_21_out, B20, Cin);
  xor xor_22 (xor_22_out, B21, Cin);
  xor xor_23 (xor_23_out, B22, Cin);
  xor xor_24 (xor_24_out, B23, Cin);
  xor xor_25 (xor_25_out, B24, Cin);
  xor xor_26 (xor_26_out, B25, Cin);
  xor xor_27 (xor_27_out, B26, Cin);
  xor xor_28 (xor_28_out, B27, Cin);
  xor xor_29 (xor_29_out, B28, Cin);
  xor xor_30 (xor_30_out, B29, Cin);
  xor xor_31 (xor_31_out, B30, Cin);
  xor xor_32 (xor_32_out, B31, Cin);
  adder_32bits adder_32bits_1 (
    .A0(A0), .B0(xor_1_out), .A1(A1), .B1(xor_2_out), .A2(A2), .B2(xor_3_out), .A3(A3), .B3(xor_4_out),
    .A4(A4), .B4(xor_5_out), .A5(A5), .B5(xor_6_out), .A6(A6), .B6(xor_7_out), .A7(A7), .B7(xor_8_out),
    .A8(A8), .B8(xor_9_out), .A9(A9), .B9(xor_10_out), .A10(A10), .B10(xor_11_out), .A11(A11),
    .B11(xor_12_out), .A12(A12), .B12(xor_13_out), .A13(A13), .B13(xor_14_out), .A14(A14), .B14(xor_15_out),
    .A15(A15), .B15(xor_16_out), .A16(A16), .B16(xor_17_out), .A17(A17), .B17(xor_18_out), .A18(A18),
    .B18(xor_19_out), .A19(A19), .B19(xor_20_out), .A20(A20), .B20(xor_21_out), .A21(A21), .B21(xor_22_out),
    .A22(A22), .B22(xor_23_out), .A23(A23), .B23(xor_24_out), .A24(A24), .B24(xor_25_out), .A25(A25),
    .B25(xor_26_out), .A26(A26), .B26(xor_27_out), .A27(A27), .B27(xor_28_out), .A28(A28), .B28(xor_29_out),
    .A29(A29), .B29(xor_30_out), .A30(A30), .B30(xor_31_out), .A31(A31), .B31(xor_32_out), .Cin(Cin),
    .O0(O0), .O1(O1), .O2(O2), .O3(O3), .O4(O4), .O5(O5), .O6(O6), .O7(O7), .O8(O8), .O9(O9), .O10(O10),
    .O11(O11), .O12(O12), .O13(O13), .O14(O14), .O15(O15), .O16(O16), .O17(O17), .O18(O18), .O19(O19),
    .O20(O20), .O21(O21), .O22(O22), .O23(O23), .O24(O24), .O25(O25), .O26(O26), .O27(O27), .O28(O28),
    .O29(O29), .O30(O30), .O31(O31), .Cout(Cout));
endmodule
